# Fritzing sketch CovidPatientAssssingDevice (saved by Fritzing 0.8.7b)
breadboards: 1

parts:
  Part3 = Triple Axis Accelerometer Breakout - ADXL335
  M1 = MAX30102
  Part4 = Arduino Nano (Rev3.0)

nets:
  N1: Part3.YOUT, Part4.A1
  GND: Part3.GND, M1.GND, Part4.GND
  VCC: Part3.VCC, M1.VIN, Part4.5V
  N2: M1.SCL, Part4.A5
  N3: M1.SDA, Part4.A4

custom parts:
  MAX30102: Oximeter module using the MAX30102 chip. You may wish to read (and check your module) this post on power problems with these modules: https://reedpaper.wordpress.com/2018/08/22/pulse-oximeter-max30100-max30102-how-to-fix-wrong-board/ . As usual, if you want the mounting holes in pcb, you need to drag a hole over the pad in silkscreen to actually drill the hole (by default they are not drilled)
